// Logisim project test 74381.circ as structural Verilog: 1 circuit, main circuit main
module main (
  input  Cn,
  input  [3:0] A,
  input  [3:0] B,
  input  [2:0] S,
  output [3:0] F,
  output P,
  output G
);

  _74381 u_74381_1 (
    .Cn(Cn), .B0(B[0]), .A0(A[0]), .B1(B[1]), .A1(A[1]), .B2(B[2]), .A2(A[2]), .B3(B[3]), .A3(A[3]),
    .S0(S[0]), .S1(S[1]), .S2(S[2]), .F0(F[0]), .F1(F[1]), .F2(F[2]), .F3(F[3]), .P(P), .G(G));
endmodule
