// Logisim project all_circuits.circ as structural Verilog: 3 circuits, main circuit part1
module part1 (
);

  LED led_1 (.in(1'b1));
  LED #(.active("false")) led_2 (.in(1'b1));
  LED led_3 (.in(1'b0));
  LED #(.active("false")) led_4 (.in(1'b0));

  // Notes on the sheet:
  //   Vcc(5V)
  //   +
  //   -
  //   Gnd(0V)
  //   Logic Monitor
  //   High
  //   Low
  //   High
  //   Low
endmodule

module part2 (
  input  Switch,
  input  Switch_2
);

  wire not_1_out, not_2_out;

  LED led_1 (.in(Switch));
  LED #(.active("false")) led_2 (.in(Switch));
  LED led_3 (.in(not_1_out));
  not not_1 (not_1_out, Switch);
  LED #(.active("false")) led_4 (.in(not_1_out));
  LED led_5 (.in(Switch_2));
  LED #(.active("false")) led_6 (.in(Switch_2));
  LED led_7 (.in(not_2_out));
  not not_2 (not_2_out, Switch_2);
  LED #(.active("false")) led_8 (.in(not_2_out));

  // Notes on the sheet:
  //   Logic Monitor
  //   Input
  //   Output
  //   High
  //   Low
  //   High
  //   Low
  //   Input
  //   Output
  //   Logic Monitor
  //   High
  //   Low
  //   High
  //   Low
endmodule

module part4 (
  input  in_1,
  input  in_2,
  input  in_3,
  input  in_4,
  input  in_5,
  input  in_6,
  input  in_7,
  input  in_8
);

  Hex_Digit_Display hex_digit_display_1 (.value({in_7, in_5, in_3, in_1}));  // open: dp
  Hex_Digit_Display hex_digit_display_2 (.value({in_8, in_6, in_4, in_2}));  // open: dp

  // Notes on the sheet:
  //   Least Significant Digit
  //   Most Significant Digit
  //   Least Significant Digit
  //   Most Significant Digit
endmodule
