// Logisim project part1.circ as structural Verilog: 1 circuit, main circuit main
module main (
);

  LED led_1 (.in(1'b1));
  LED #(.active("false")) led_2 (.in(1'b1));
  LED led_3 (.in(1'b0));
  LED #(.active("false")) led_4 (.in(1'b0));

  // Notes on the sheet:
  //   Vcc(5V)
  //   +
  //   -
  //   Gnd(0V)
  //   Logic Monitor
  //   High
  //   Low
  //   High
  //   Low
endmodule
