// Logisim project part4.circ as structural Verilog: 1 circuit, main circuit main
module main (
  input  in_1,
  input  in_2,
  input  in_3,
  input  in_4,
  input  in_5,
  input  in_6,
  input  in_7,
  input  in_8
);

  Hex_Digit_Display hex_digit_display_1 (.value({in_7, in_5, in_3, in_1}));  // open: dp
  Hex_Digit_Display hex_digit_display_2 (.value({in_8, in_6, in_4, in_2}));  // open: dp
endmodule
