// Logisim project part1-f1.circ as structural Verilog: 1 circuit, main circuit main
module main (
  input  a,
  input  b
);

  wire and_1_out, or_1_out;

  and and_1 (and_1_out, a, b);
  or or_1 (or_1_out, a, and_1_out);
  LED led_1 (.in(or_1_out));

  // Notes on the sheet:
  //   F
  //   1
endmodule
