// Logisim project part1-f2.circ as structural Verilog: 5 circuits, main circuit part1-f2
module part1_f2 (
  input  a,
  input  b
);

  wire and_1_out, not_1_out, or_1_out, or_2_out;

  not not_1 (not_1_out, b);
  or or_1 (or_1_out, a, b);
  or or_2 (or_2_out, a, not_1_out);
  and and_1 (and_1_out, or_1_out, or_2_out);
  LED led_1 (.in(and_1_out));
  LED #(.active("false")) led_2 (.in(and_1_out));

  // Notes on the sheet:
  //   Switches
  //   a
  //   b
  //   Logic Monitor
  //   F
  //   2
  //   High
  //   Low
endmodule

module part1_f1 (
  input  a,
  input  b
);

  wire and_1_out, or_1_out;

  and and_1 (and_1_out, a, b);
  or or_1 (or_1_out, a, and_1_out);
  LED led_1 (.in(or_1_out));
  LED #(.active("false")) led_2 (.in(or_1_out));

  // Notes on the sheet:
  //   Switches
  //   Logic Monitor
  //   F
  //   1
  //   High
  //   Low
endmodule

module part2 (
  input  a,
  input  b
);

  wire and_1_out, or_1_out;

  or or_1 (or_1_out, a, b);
  LED led_1 (.in(and_1_out));
  and and_1 (and_1_out, or_1_out, a);
  LED #(.active("false")) led_2 (.in(and_1_out));
  LED led_3 (.in(a));
  LED #(.active("false")) led_4 (.in(a));

  // Notes on the sheet:
  //   Switches
  //   a
  //   b
  //   a
  //   Logic Monitor
  //   a * (a+b) 
  //   High
  //   Low
  //   High
  //   Low
endmodule

module part3 (
  input  a,
  input  b,
  input  c
);

  wire and_1_out, not_1_out, not_2_out, not_3_out, or_1_out, or_2_out;

  not not_1 (not_1_out, a);
  not not_2 (not_2_out, b);
  not not_3 (not_3_out, c);
  or or_1 (or_1_out, not_1_out, not_2_out);
  or or_2 (or_2_out, a, not_3_out);
  and and_1 (and_1_out, or_1_out, or_2_out);
  LED led_1 (.in(and_1_out));
  LED #(.active("false")) led_2 (.in(and_1_out));

  // Notes on the sheet:
  //   a
  //   a'
  //   a'
  //   c
  //   b
  //   Logic Monitor
  //   F' = (a' + b') * (a + c')
  //   High
  //   Low
endmodule

module part4 (
  input  c,
  input  d
);

  wire and_1_out, and_2_out, not_1_out, not_2_out, or_1_out;

  not not_1 (not_1_out, c);
  not not_2 (not_2_out, d);
  and and_1 (and_1_out, not_1_out, d);
  and and_2 (and_2_out, c, not_2_out);
  or or_1 (or_1_out, and_1_out, and_2_out);
  LED led_1 (.in(or_1_out));
  LED #(.active("false")) led_2 (.in(or_1_out));

  // Notes on the sheet:
  //   Switches
  //   Logic Monitor
  //   (c' * d) + (c * d')
  //   High
  //   Low
endmodule
