// Logisim project part2.circ as structural Verilog: 1 circuit, main circuit main
module main (
  input  a,
  input  b
);

  wire and_1_out, or_1_out;

  or or_1 (or_1_out, a, b);
  and and_1 (and_1_out, or_1_out, a);
  LED led_1 (.in(and_1_out));
  LED led_2 (.in(a));

  // Notes on the sheet:
  //   a * (a+b) 
  //   a
endmodule
