// Logisim project part3.circ as structural Verilog: 1 circuit, main circuit main
module main (
  input  a,
  input  b,
  input  c
);

  wire and_1_out, not_1_out, not_2_out, not_3_out, or_1_out, or_2_out;

  not not_1 (not_1_out, b);
  not not_2 (not_2_out, c);
  not not_3 (not_3_out, a);
  or or_1 (or_1_out, not_3_out, not_1_out);
  or or_2 (or_2_out, a, not_2_out);
  and and_1 (and_1_out, or_1_out, or_2_out);
  LED led_1 (.in(and_1_out));

  // Notes on the sheet:
  //   a
  //   a'
  //   a'
  //   b
  //   c
  //   F' = (a' + b') * (a + c')
endmodule
