// Logisim project part4.circ as structural Verilog: 1 circuit, main circuit main
module main (
  input  c,
  input  d,
  output f
);

  wire and_1_out, and_2_out, not_1_out, not_2_out;

  not not_1 (not_1_out, c);
  and and_1 (and_1_out, not_1_out, d);
  and and_2 (and_2_out, c, not_2_out);
  not not_2 (not_2_out, d);
  or or_1 (f, and_1_out, and_2_out);
endmodule
