// Logisim project Circuits.circ as structural Verilog: 7 circuits, main circuit part1
module part2 (
  input  a,
  input  b,
  input  c,
  input  d
);

  wire nand_1_out, nand_2_out, nand_3_out, nand_4_out, nand_5_out, nand_6_out, not_1_out, not_2_out,
       not_3_out, not_4_out, not_5_out, not_6_out;

  not not_1 (not_1_out, a);
  not not_2 (not_2_out, b);
  not not_3 (not_3_out, c);
  not not_4 (not_4_out, c);
  not not_5 (not_5_out, d);
  nand nand_1 (nand_1_out, not_1_out, not_2_out, not_3_out);
  nand nand_2 (nand_2_out, c, d);
  nand nand_3 (nand_3_out, b, d);
  nand nand_4 (nand_4_out, a, not_4_out, not_5_out);
  not not_6 (not_6_out, nand_5_out);
  nand nand_5 (nand_5_out, nand_1_out, nand_2_out, nand_3_out);
  nand nand_6 (nand_6_out, not_6_out, nand_4_out);
  LED led_1 (.in(nand_6_out));
  LED #(.active("false")) led_2 (.in(nand_6_out));

  // Notes on the sheet:
  //   Switches
  //   Logic Monitor
  //   F(a,b,c,d)
  //   High
  //   Low
endmodule

module part1 (
  input  a,
  input  b,
  input  c,
  input  d
);

  wire and_1_out, and_2_out, and_3_out, and_4_out, not_1_out, not_2_out, not_3_out, not_4_out, not_5_out,
       or_1_out, or_2_out, or_3_out;

  not not_1 (not_1_out, a);
  not not_2 (not_2_out, b);
  not not_3 (not_3_out, c);
  not not_4 (not_4_out, c);
  not not_5 (not_5_out, d);
  and and_1 (and_1_out, not_1_out, not_2_out, not_3_out);
  and and_2 (and_2_out, c, d);
  and and_3 (and_3_out, b, d);
  and and_4 (and_4_out, a, not_4_out, not_5_out);
  or or_1 (or_1_out, and_1_out, and_2_out);
  or or_2 (or_2_out, and_3_out, and_4_out);
  LED led_1 (.in(or_3_out));
  or or_3 (or_3_out, or_1_out, or_2_out);
  LED #(.active("false")) led_2 (.in(or_3_out));

  // Notes on the sheet:
  //   Switches
  //   Logic Monitor
  //   F(a,b,c,d)
  //   High
  //   Low
endmodule

module part3 (
  input  a,
  input  b,
  input  c,
  input  d
);

  wire multiplexer_1_out, not_1_out;

  not not_1 (not_1_out, d);
  Multiplexer #(.select(3), .enable("false")) multiplexer_1 (
    .in0(1'b1), .in1(d), .in2(d), .in3(d), .in4(1'b0), .in5(d), .in6(1'b1), .in7(1'b0),
    .out(multiplexer_1_out), .sel({a, b, c}));
  LED led_1 (.in(multiplexer_1_out));
  LED #(.active("false")) led_2 (.in(multiplexer_1_out));

  // Notes on the sheet:
  //   Switches
  //   1
  //   d
  //   0
  //   d'
  //   Logic Monitor
  //   F(a,b,c,d)
  //   High
  //   Low
endmodule

module part4 (
  input  a,
  input  b,
  input  c
);

  wire decoder_1_out_2, decoder_1_out_4, decoder_1_out_5, decoder_1_out_9, not_1_out, not_2_out, not_3_out,
       not_4_out, or_1_out, or_2_out, or_3_out;

  decoder decoder_1 (
    .in_1({a, b, c}), .out_2(decoder_1_out_2), .out_4(decoder_1_out_4), .out_5(decoder_1_out_5),
    .out_9(decoder_1_out_9));  // open: out_3, out_6, out_7, out_8
  not not_1 (not_1_out, decoder_1_out_2);
  not not_2 (not_2_out, decoder_1_out_4);
  not not_3 (not_3_out, decoder_1_out_5);
  not not_4 (not_4_out, decoder_1_out_9);
  or or_1 (or_1_out, not_1_out, not_2_out);
  or or_2 (or_2_out, or_1_out, or_3_out);
  or or_3 (or_3_out, not_3_out, not_4_out);
  LED led_1 (.in(or_2_out));
  LED #(.active("false")) led_2 (.in(or_2_out));

  // Notes on the sheet:
  //   Switches
  //   Logic Monitor
  //   F1
  //   High
  //   Low
endmodule

module decoder (
  input  [2:0] in_1,
  output out_2,
  output out_3,
  output out_4,
  output out_5,
  output out_6,
  output out_7,
  output out_8,
  output out_9
);

  wire decoder_1_out0, decoder_1_out1, decoder_1_out2, decoder_1_out3, decoder_1_out4, decoder_1_out5,
       decoder_1_out6, decoder_1_out7;

  not not_1 (out_2, decoder_1_out0);
  not not_2 (out_3, decoder_1_out1);
  not not_3 (out_4, decoder_1_out2);
  not not_4 (out_5, decoder_1_out3);
  not not_5 (out_6, decoder_1_out4);
  not not_6 (out_7, decoder_1_out5);
  not not_7 (out_8, decoder_1_out6);
  not not_8 (out_9, decoder_1_out7);
  Decoder #(.select(3), .enable("false")) decoder_1 (
    .out0(decoder_1_out0), .out1(decoder_1_out1), .out2(decoder_1_out2), .out3(decoder_1_out3),
    .out4(decoder_1_out4), .out5(decoder_1_out5), .out6(decoder_1_out6), .out7(decoder_1_out7), .sel(in_1));
endmodule

module part4_f2 (
  input  a,
  input  b,
  input  c
);

  wire decoder_1_out_2, decoder_1_out_8, decoder_1_out_9, not_1_out, not_2_out, not_3_out, or_1_out, or_2_out;

  decoder decoder_1 (
    .in_1({a, b, c}), .out_2(decoder_1_out_2), .out_8(decoder_1_out_8), .out_9(decoder_1_out_9));  // open: out_3, out_4, out_5, out_6, out_7
  not not_1 (not_1_out, decoder_1_out_2);
  not not_2 (not_2_out, decoder_1_out_8);
  or or_1 (or_1_out, not_2_out, not_3_out);
  not not_3 (not_3_out, decoder_1_out_9);
  or or_2 (or_2_out, not_1_out, or_1_out);
  LED led_1 (.in(or_2_out));
  LED #(.active("false")) led_2 (.in(or_2_out));

  // Notes on the sheet:
  //   Switches
  //   Logic Monitor
  //   F2
  //   High
  //   Low
endmodule

module fakayu (
  input  a,
  input  b,
  input  c,
  input  d,
  output f
);

  wire and_1_out, and_2_out, and_3_out, and_4_out, and_5_out, not_1_out, not_2_out, not_3_out, not_4_out,
       not_5_out, not_6_out, not_7_out;

  not not_1 (not_1_out, a);
  and and_1 (and_1_out, not_1_out, not_2_out, not_3_out);
  not not_2 (not_2_out, b);
  not not_3 (not_3_out, c);
  not not_4 (not_4_out, a);
  and and_2 (and_2_out, not_4_out, d);
  not not_5 (not_5_out, b);
  and and_3 (and_3_out, not_5_out, c, d);
  and and_4 (and_4_out, a, b, not_6_out);
  not not_6 (not_6_out, c);
  and and_5 (and_5_out, a, b, not_7_out);
  not not_7 (not_7_out, d);
  or or_1 (f, and_1_out, and_2_out, and_3_out, and_4_out, and_5_out);
endmodule
