// Logisim project exp.circ as structural Verilog: 4 circuits, main circuit part1
module part1 (
  input  A,
  input  B
);

  wire and_1_out, xor_1_out;

  xor xor_1 (xor_1_out, A, B);
  and and_1 (and_1_out, A, B);
  LED led_1 (.in(xor_1_out));
  LED #(.active("false")) led_2 (.in(xor_1_out));
  LED led_3 (.in(and_1_out));
  LED #(.active("false")) led_4 (.in(and_1_out));

  // Notes on the sheet:
  //   Logic Monitor
  //   Sum
  //   High
  //   Low
  //   Carry
  //   High
  //   Low
endmodule

module part2 (
  input  C_in,
  input  A,
  input  B
);

  wire and_1_out, and_2_out, or_1_out, xor_1_out, xor_2_out;

  xor xor_1 (xor_1_out, A, B);
  and and_1 (and_1_out, A, B);
  xor xor_2 (xor_2_out, C_in, xor_1_out);
  and and_2 (and_2_out, C_in, xor_1_out);
  LED led_1 (.in(xor_2_out));
  LED #(.active("false")) led_2 (.in(xor_2_out));
  LED led_3 (.in(or_1_out));
  or or_1 (or_1_out, and_2_out, and_1_out);
  LED #(.active("false")) led_4 (.in(or_1_out));

  // Notes on the sheet:
  //   Logic Monitor
  //   Sum
  //   Carry
  //   High
  //   Low
  //   High
  //   Low
endmodule

module part3 (
  input  Add_Subtract,
  input  B0,
  input  B1,
  input  B2,
  input  B3,
  input  A0,
  input  A1,
  input  A2,
  input  A3
);

  wire adder_1_cout;
  wire [3:0] adder_1_out, xor_1_out;

  xor xor_1 (xor_1_out[0], B0, Add_Subtract);
  xor xor_2 (xor_1_out[1], B1, Add_Subtract);
  xor xor_3 (xor_1_out[2], B2, Add_Subtract);
  xor xor_4 (xor_1_out[3], B3, Add_Subtract);
  Adder #(.width(4)) adder_1 (
    .a(xor_1_out), .b({A3, A2, A1, A0}), .out(adder_1_out), .cin(Add_Subtract), .cout(adder_1_cout));
  LED led_1 (.in(adder_1_out[0]));
  LED #(.active("false")) led_2 (.in(adder_1_out[0]));
  LED led_3 (.in(adder_1_out[1]));
  LED #(.active("false")) led_4 (.in(adder_1_out[1]));
  LED led_5 (.in(adder_1_out[2]));
  LED #(.active("false")) led_6 (.in(adder_1_out[2]));
  LED led_7 (.in(adder_1_out[3]));
  LED #(.active("false")) led_8 (.in(adder_1_out[3]));
  LED led_9 (.in(adder_1_cout));
  LED #(.active("false")) led_10 (.in(adder_1_cout));

  // Notes on the sheet:
  //   Logic Monitor
  //   C0
  //   High
  //   Low
  //   C1
  //   High
  //   Low
  //   C2
  //   High
  //   Low
  //   C3
  //   High
  //   Low
  //   Carry Out
  //   High
  //   Low
endmodule

module part4 (
  input  B0,
  input  B1,
  input  B2,
  input  B3,
  input  S0,
  input  S1,
  input  S2,
  input  s3,
  input  M,
  input  in_10,
  input  Clear
);

  wire n74181_1_p2, n74181_1_p9, n74181_1_p10, n74181_1_p11, n74181_1_p12, n74181_1_p14, n74181_1_p16,
       n74181_1_p18, n74181_1_p19, n74181_1_p20, n74181_1_p21, not_1_out, not_2_out, not_3_out, not_4_out;

  // _74181 74181_1: pin names not known; wires that end beside it: B0, n74181_1_p2, s3, S2, S1, S0, 1'b0, M, n74181_1_p9, n74181_1_p10, n74181_1_p11, n74181_1_p12, B1, n74181_1_p14, B2, n74181_1_p16, B3, n74181_1_p18, n74181_1_p19, n74181_1_p20, n74181_1_p21, n74181_1_p18, n74181_1_p20
  D_Flip_Flop d_ff_1 (.clk(in_10), .D(n74181_1_p21), .Q(n74181_1_p16), .reset(Clear));  // open: Qn, preset, en
  D_Flip_Flop d_ff_2 (.clk(in_10), .D(n74181_1_p11), .Q(n74181_1_p14), .reset(Clear));  // open: Qn, preset, en
  D_Flip_Flop d_ff_3 (.clk(in_10), .D(n74181_1_p10), .Q(n74181_1_p12), .reset(Clear));  // open: Qn, preset, en
  D_Flip_Flop d_ff_4 (.clk(in_10), .D(n74181_1_p9), .Q(n74181_1_p2), .reset(Clear));  // open: Qn, preset, en
  not not_1 (not_1_out, n74181_1_p16);
  not not_2 (not_2_out, n74181_1_p14);
  not not_3 (not_3_out, n74181_1_p12);
  not not_4 (not_4_out, n74181_1_p2);
  LED led_1 (.in(not_1_out));
  LED #(.active("false")) led_2 (.in(not_1_out));
  LED led_3 (.in(not_2_out));
  LED #(.active("false")) led_4 (.in(not_2_out));
  LED led_5 (.in(not_3_out));
  LED #(.active("false")) led_6 (.in(not_3_out));
  LED led_7 (.in(not_4_out));
  LED #(.active("false")) led_8 (.in(not_4_out));
  LED led_9 (.in(n74181_1_p19));
  LED #(.active("false")) led_10 (.in(n74181_1_p19));

  // Notes on the sheet:
  //   (F3)'
  //   (F0)'
  //   (A1)'
  //   (A3)'
  //   Clock simulating switch
  //   (F3)'
  //   (F0)'
  //   Logic Monitor
  //   F3
  //   High
  //   Low
  //   F2
  //   High
  //   Low
  //   F1
  //   High
  //   Low
  //   F0
  //   High
  //   Low
  //   High
  //   Low
endmodule
