// Logisim project Circuits.circ as structural Verilog: 5 circuits, main circuit part1
module part1 (
  input  S,
  input  R
);

  wire nor_1_out, nor_2_out;

  nor nor_1 (nor_1_out, S, nor_2_out);
  nor nor_2 (nor_2_out, nor_1_out, R);
  LED led_1 (.in(nor_1_out));
  LED #(.active("false")) led_2 (.in(nor_1_out));
  LED led_3 (.in(nor_2_out));
  LED #(.active("false")) led_4 (.in(nor_2_out));

  // Notes on the sheet:
  //   S-R Latch
  //   _
  //   Q
  //   Q
  //   Logic Monitor
  //   High
  //   Low
  //   High
  //   Low
endmodule

module part2 (
  input  S,
  input  C,
  input  R
);

  wire nand_1_out, nand_2_out, nand_3_out, nand_4_out;

  nand nand_1 (nand_1_out, S, C);
  nand nand_2 (nand_2_out, C, R);
  nand nand_3 (nand_3_out, nand_1_out, nand_4_out);
  nand nand_4 (nand_4_out, nand_3_out, nand_2_out);
  LED led_1 (.in(nand_3_out));
  LED #(.active("false")) led_2 (.in(nand_3_out));
  LED led_3 (.in(nand_4_out));
  LED #(.active("false")) led_4 (.in(nand_4_out));

  // Notes on the sheet:
  //   Logic Monitor
  //   Q
  //   _
  //   Q
  //   High
  //   Low
  //   High
  //   Low
endmodule

module part3 (
  input  D
);

  wire clock_1_out, not_1_out, part3_dflipflop_1_q, part3_dflipflop_2_q, part3_dflipflop_2_q_2;

  Clock clock_1 (.out(clock_1_out));
  part3_dflipflop part3_dflipflop_1 (.d(D), .C(clock_1_out), .Q(part3_dflipflop_1_q));  // open: Q_2
  not not_1 (not_1_out, clock_1_out);
  part3_dflipflop part3_dflipflop_2 (
    .d(part3_dflipflop_1_q), .C(not_1_out), .Q(part3_dflipflop_2_q), .Q_2(part3_dflipflop_2_q_2));
  LED led_1 (.in(part3_dflipflop_2_q));
  LED #(.active("false")) led_2 (.in(part3_dflipflop_2_q));
  LED led_3 (.in(part3_dflipflop_2_q_2));
  LED #(.active("false")) led_4 (.in(part3_dflipflop_2_q_2));

  // Notes on the sheet:
  //   CLK
  //   Logic Monitor
  //   Q
  //   _
  //   Q
  //   High
  //   Low
  //   Low
  //   High
endmodule

module part3_dflipflop (
  input  d,
  input  C,
  output Q,
  output Q_2
);

  wire nand_1_out, nand_2_out, not_1_out;

  not not_1 (not_1_out, d);
  nand nand_1 (nand_1_out, d, C);
  nand nand_2 (nand_2_out, C, not_1_out);
  nand nand_3 (Q, nand_1_out, Q_2);
  nand nand_4 (Q_2, Q, nand_2_out);

  // Notes on the sheet:
  //   _
endmodule

module part4 (
  input  in_1,
  input  I4,
  input  I3,
  input  I5,
  input  I2,
  input  I6,
  input  I1,
  input  I7,
  input  I0
);

  wire clock_1_out, n74165_1_p12;

  Clock clock_1 (.out(clock_1_out));
  // _74165 74165_1: pin names not known; wires that end beside it: in_1, clock_1_out, I4, I5, I6, I7, 1'b0, I3, I2, I1, I0, n74165_1_p12, n74165_1_p12

  // Notes on the sheet:
  //   Shift/Load
  //   CLK
  //   CLK INH
endmodule
