// Logisim project exp8.circ as structural Verilog: 3 circuits, main circuit part1
module part1 (
  input  X
);

  wire and_1_out, button_1_out, d_ff_1_q, d_ff_1_qn, d_ff_2_q, d_ff_2_qn, or_1_out, or_2_out;

  Button button_1 (.out(button_1_out));
  D_Flip_Flop d_ff_1 (
    .clk(button_1_out), .D(or_1_out), .Q(d_ff_1_q), .Qn(d_ff_1_qn), .en(1'b1));  // open: preset, reset
  or or_1 (or_1_out, d_ff_2_q, d_ff_1_qn);
  D_Flip_Flop d_ff_2 (
    .clk(button_1_out), .D(and_1_out), .Q(d_ff_2_q), .Qn(d_ff_2_qn), .en(1'b1));  // open: preset, reset
  and and_1 (and_1_out, X, d_ff_2_qn);
  LED led_1 (.in(or_2_out));
  or or_2 (or_2_out, d_ff_1_q, d_ff_2_qn);
  LED #(.active("false")) led_2 (.in(or_2_out));

  // Notes on the sheet:
  //   CLK
  //   Q0
  //   D0
  //   Q1
  //   D1
  //   Y
  //   Logic Monitor
  //   High
  //   Low
endmodule

module part2 (
  input  X
);

  wire and_1_out, and_2_out, and_3_out, and_4_out, and_5_out, button_1_out, d_ff_1_q, d_ff_1_qn, d_ff_2_q,
       d_ff_2_qn, not_1_out, or_1_out, or_2_out;

  not not_1 (not_1_out, X);
  and and_1 (and_1_out, d_ff_1_qn, d_ff_2_qn);
  and and_2 (and_2_out, d_ff_2_q, not_1_out);
  and and_3 (and_3_out, X, and_1_out);
  and and_4 (and_4_out, and_1_out, not_1_out);
  and and_5 (and_5_out, X, d_ff_1_q);
  or or_1 (or_1_out, and_2_out, and_3_out);
  or or_2 (or_2_out, and_4_out, and_5_out);
  Button button_1 (.out(button_1_out));
  D_Flip_Flop d_ff_1 (
    .clk(button_1_out), .D(or_1_out), .Q(d_ff_1_q), .Qn(d_ff_1_qn), .en(1'b1));  // open: preset, reset
  D_Flip_Flop d_ff_2 (
    .clk(button_1_out), .D(or_2_out), .Q(d_ff_2_q), .Qn(d_ff_2_qn), .en(1'b1));  // open: preset, reset
  LED led_1 (.in(d_ff_1_q));
  LED #(.active("false")) led_2 (.in(d_ff_1_q));
  LED led_3 (.in(d_ff_2_q));
  LED #(.active("false")) led_4 (.in(d_ff_2_q));

  // Notes on the sheet:
  //   __
  //   __
  //   X
  //   X
  //   Q0
  //   __
  //   Q1
  //   Q0
  //   Q1
  //   CLK
  //   D0
  //   D1
  //   Q0
  //   Q1
  //   Logic Monitor
  //   High
  //   Low
  //   High
  //   Low
endmodule

module part3 (
  input  LSB,
  input  in_2,
  input  in_3,
  input  MSB,
  input  Increment___Load
);

  wire and_1_out, button_1_out, not_1_out;
  wire [3:0] n74161_1_p8;

  Button button_1 (.out(button_1_out));
  not not_1 (not_1_out, and_1_out);
  // _74161 74161_1: pin names not known; wires that end beside it: not_1_out, button_1_out, LSB, in_2, in_3, MSB, 1'b1, n74161_1_p8[0], n74161_1_p8[1], n74161_1_p8[2], n74161_1_p8[3], 1'b1, Increment___Load
  and and_1 (and_1_out, n74161_1_p8[1], n74161_1_p8[2]);
  Hex_Digit_Display hex_digit_display_1 (.value(n74161_1_p8));  // open: dp

  // Notes on the sheet:
  //   CLK
  //   ____
endmodule
