// Logisim project all_circuits.circ as structural Verilog: 2 circuits, main circuit ALU
module ALU (
  input  A,
  input  B,
  input  Cin,
  input  s2,
  input  s1,
  input  s0,
  output Cout,
  output out_8
);

  wire adder_1_cout, adder_1_out, and_1_out, and_2_out, and_3_out, not_1_out, not_2_out, xor_1_out,
       xor_2_out, xor_3_out;

  xor xor_1 (xor_1_out, B, s0);
  not not_1 (not_1_out, A);
  Adder #(.width(1)) adder_1 (.a(A), .b(xor_1_out), .out(adder_1_out), .cin(Cin), .cout(adder_1_cout));
  xor xor_2 (xor_2_out, A, B);
  xor xor_3 (xor_3_out, not_1_out, Cin);
  and and_1 (and_1_out, not_1_out, Cin);
  not not_2 (not_2_out, s2);
  and and_2 (and_2_out, adder_1_cout, not_2_out);
  and and_3 (and_3_out, and_1_out, s2);
  Multiplexer #(.select(3), .enable("false")) multiplexer_1 (
    .in0(adder_1_out), .in1(adder_1_out), .in2(xor_2_out), .in3(1'b0), .in4(not_1_out), .in5(xor_3_out),
    .in6(B), .out(out_8), .sel({s2, s1, s0}));  // open: in7
  or or_1 (Cout, and_2_out, and_3_out);

  // Notes on the sheet:
  //   s0
  //   __
  //   s2
  //   s2
endmodule

module _4b (
  input  cin,
  input  b,
  input  in_3,
  input  in_4,
  input  in_5
);

  wire alu_1_cout, alu_1_out_8, clock_1_out, d_ff_1_q, d_ff_2_q, d_ff_3_q, d_ff_4_q, d_ff_5_q, or_1_out;

  or or_1 (or_1_out, d_ff_1_q, cin);
  ALU alu_1 (
    .Cout(alu_1_cout), .A(d_ff_5_q), .B(b), .Cin(or_1_out), .s2(in_3), .s1(in_4), .s0(in_5),
    .out_8(alu_1_out_8));
  D_Flip_Flop d_ff_1 (.clk(clock_1_out), .D(alu_1_cout), .Q(d_ff_1_q), .en(1'b1));  // open: Qn, preset, reset
  D_Flip_Flop d_ff_2 (.clk(clock_1_out), .D(alu_1_out_8), .Q(d_ff_2_q), .en(1'b1));  // open: Qn, preset, reset
  D_Flip_Flop d_ff_3 (.clk(clock_1_out), .D(d_ff_2_q), .Q(d_ff_3_q), .en(1'b1));  // open: Qn, preset, reset
  D_Flip_Flop d_ff_4 (.clk(clock_1_out), .D(d_ff_3_q), .Q(d_ff_4_q), .en(1'b1));  // open: Qn, preset, reset
  D_Flip_Flop d_ff_5 (.clk(clock_1_out), .D(d_ff_4_q), .Q(d_ff_5_q), .en(1'b1));  // open: Qn, preset, reset
  Clock clock_1 (.out(clock_1_out));

  // Notes on the sheet:
  //   q0
  //   MSB
  //   LSB
endmodule
